# Fritzing sketch ooo_office_v0-2 (saved by Fritzing 0.8.3b)
breadboards: 1

parts:
  Part1 = Arduino Uno (Rev3)
  R1 = Resistor [tolerance=±5% resistance=10k package=THT]
  R2 = Resistor [tolerance=±5% resistance=220 package=THT]
  J1 = Basic Force Sensing Resistor (FSR) [package=THT]
  J2 = Basic Force Sensing Resistor (FSR) [package=THT]

nets:
  N1: Part1.A0, R1.Pin_1, J1.pin_0
  N2: Part1.A1, R2.Pin_1, J2.pin_0
